# Fritzing sketch Drop of Life (saved by Fritzing 0.9.2b)

parts:
  Part1 = HT16K33 Breakout 16x8 LED Matrix Driver [part_number=1427]
  Part2 = Photon

nets:
  N1: Part1.SCL, Part2.D1, Part2.D2
  N2: Part1.SDA, Part2.D0
  VDD: Part1.VDD, Part2.3V3
  GND: Part1.GND, Part2.GND

custom parts:
  HT16K33 Breakout 16x8 LED Matrix Driver: This is the magic sauce in our 7-segment and matrix backpacks, now available in breadboard-friendly breakout board format. The HT16K33 is a neat little chip that has the ability to drive a multiplexed 16x8 matrix (that's 128 individual LEDs). The communication protocol is I2C so it uses only 2 pins, and you can have up to 8 selectable I2C addresses so thats a total of 8 matrices, each one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
